# Fritzing sketch Keypad-v2 (saved by Fritzing 0.9.3b)
circuit board: 6.87869cm x 4.32648cm
breadboards: 1

parts:
  C = Pushbutton [package="[THT]"]
  D = Pushbutton [package="[THT]"]
  E = Pushbutton [package="[THT]"]
  A = Pushbutton [package="[THT]"]
  B = Pushbutton [package="[THT]"]
  P0 = Toggle Switch [package=THT]
  P1 = Toggle Switch [package=THT]
  DIP = DIP Switch 4 Position [package=dipswitch-04]
  J1 = female pin header, 3 pins [form="♀ (female)"]
  23008 = IC, DIP package, 18 pins [chip_label=MCP23008]
  32u4_BLE = Modified Adafruit Feather 32u4 Bluefruit [part_number="Adafruit #2829"]

nets:
  N1: C.Pin_1, C.Pin_2, 32u4_BLE.5
  N2: C.Pin_3, C.Pin_4, D.Pin_3, D.Pin_4, E.Pin_3, E.Pin_4, A.Pin_3, A.Pin_4, B.Pin_3, B.Pin_4, P0.COM, P1.COM, DIP.1, DIP.2, DIP.3, DIP.4, J1.pin1, 23008.pin3, 23008.pin4, 23008.pin5, 23008.pin9, 32u4_BLE.GND
  N3: D.Pin_1, D.Pin_2, 32u4_BLE.10
  N4: E.Pin_1, E.Pin_2, 23008.pin10
  N5: A.Pin_1, A.Pin_2, 32u4_BLE.6
  N6: B.Pin_1, B.Pin_2, 32u4_BLE.9
  N7: P0.L2, 23008.pin16
  N8: P1.L2, 23008.pin17
  N9: DIP.5, 23008.pin14
  N10: DIP.6, 23008.pin13
  N11: DIP.7, 23008.pin12
  N12: DIP.8, 23008.pin11
  N13: J1.pin2, 32u4_BLE.12
  N14: J1.pin3, 32u4_BLE.11
  N15: 23008.pin1, 32u4_BLE.3
  N16: 23008.pin2, 32u4_BLE.2
  N17: 23008.pin6, 23008.pin18, 32u4_BLE.+3V3

notes:
  GND
  RXD/TXD
  Parc Keypad v2r1 (C)

custom parts:
  Modified Adafruit Feather 32u4 Bluefruit: This is the Adafruit Feather 32u4 Bluefruit - our take on an 'all-in-one' Arduino-compatible + Bluetooth Low Energy with built in USB and battery charging. Its an Adafruit Feather 32u4 with a BTLE module, ready to rock! We have other boards in the Feather family, check'em out here. Bluetooth Low Energy is the hottest new low-power, 2.4GHz spectrum wireless protocol. In particular, its the only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
